// Logisim project Proiect_ceas_cu_radio_programabil.circ as structural Verilog
module main (
  output out_1,
  output [5:0] out_2
);

  wire Alarma_out, clock_1_out, comp_5b_1_cmp_5b, comp_6b_1_cmp_6b, Min_out, num_secunde_1_enable,
       numarator_60_1_enable_24, Ok_out, Oprire_out, Ora_out, poarta_nu_1_b, poarta_sau_1_out_sau,
       poarta_sau_2_out_sau, poarta_sau_3_out_sau, poarta_sau_4_out_sau, poarta_sau_5_out_sau,
       poarta_sau_6_out_sau, poarta_si_1_si_out, poarta_si_2_si_out, Pornire_out, Radio_out, Reset_out,
       Ring_out, Setare_ora_out, unitate_centrala_1_alarma_set, unitate_centrala_1_cresc_24,
       unitate_centrala_1_cresc_60, unitate_centrala_1_en_set_al, unitate_centrala_1_en_set_ora,
       unitate_centrala_1_led_on, unitate_centrala_1_led_radio, unitate_centrala_1_ok_set_al;
  wire [3:0] convertor_1_decimal, convertor_1_unit, convertor_2_decimal, convertor_2_unit;
  wire [4:0] mux_2_la_1_5b_1_out5, Num_24_alarma_out_24, Num_24_ora_out_24, registru_5biti_1_out_5;
  wire [5:0] mux_2_la_1_6b_1_out6, Num_60_alarma_out_60, numarator_60_1_out_60, registru_6biti_1_out_6;
  wire [6:0] hex2_7seg_1_a_b_c_d_e_f_g, hex2_7seg_2_a_b_c_d_e_f_g, hex2_7seg_3_a_b_c_d_e_f_g,
       hex2_7seg_4_a_b_c_d_e_f_g;

  Button Oprire (.out(Oprire_out));
  Button Ora (.out(Ora_out));
  Button Min (.out(Min_out));
  Clock clock_1 (.out(clock_1_out));
  Button Pornire (.out(Pornire_out));
  Button Setare_ora (.out(Setare_ora_out));
  Button Alarma (.out(Alarma_out));
  Button Radio (.out(Radio_out));
  Button Ok (.out(Ok_out));
  Button Reset (.out(Reset_out));
  Button Ring (.out(Ring_out));
  Poarta_sau poarta_sau_1 (.in1(Reset_out), .in2(Oprire_out), .out_sau(poarta_sau_1_out_sau));
  poarta_nu poarta_nu_1 (.a(unitate_centrala_1_en_set_ora), .b(poarta_nu_1_b));
  unitate_centrala unitate_centrala_1 (
    .pornire(Pornire_out), .oprire(Oprire_out), .setare_ora(Setare_ora_out), .alarma(Alarma_out),
    .radio(Radio_out), .ok(Ok_out), .reset(Reset_out), .ora(Ora_out), .minut(Min_out), .clk(clock_1_out),
    .ring(Ring_out), .led_radio(unitate_centrala_1_led_radio), .en_set_al(unitate_centrala_1_en_set_al),
    .en_set_ora(unitate_centrala_1_en_set_ora), .cresc_60(unitate_centrala_1_cresc_60),
    .cresc_24(unitate_centrala_1_cresc_24), .ok_set_al(unitate_centrala_1_ok_set_al),
    .led_on(unitate_centrala_1_led_on), .alarma_set(unitate_centrala_1_alarma_set));
  LED Pornit (.in(unitate_centrala_1_led_on));
  LED Alarma_set (.in(unitate_centrala_1_alarma_set));
  Poarta_si poarta_si_1 (
    .in1(unitate_centrala_1_led_on), .in2(clock_1_out), .in3(poarta_nu_1_b), .si_out(poarta_si_1_si_out));
  LED Radio_sunet (.in(unitate_centrala_1_led_radio));
  Poarta_sau poarta_sau_2 (
    .in1(poarta_sau_1_out_sau), .in2(unitate_centrala_1_en_set_ora), .out_sau(poarta_sau_2_out_sau));
  Poarta_sau poarta_sau_3 (
    .in1(unitate_centrala_1_en_set_ora), .in2(num_secunde_1_enable), .out_sau(poarta_sau_3_out_sau));
  Poarta_sau poarta_sau_4 (
    .in1(unitate_centrala_1_cresc_60), .in2(num_secunde_1_enable), .out_sau(poarta_sau_4_out_sau));
  Poarta_sau poarta_sau_5 (
    .in1(numarator_60_1_enable_24), .in2(unitate_centrala_1_cresc_24), .out_sau(poarta_sau_5_out_sau));
  num_secunde num_secunde_1 (
    .clk(poarta_si_1_si_out), .reset(poarta_sau_2_out_sau), .enable(num_secunde_1_enable), .out_60(out_2));
  Poarta_sau poarta_sau_6 (
    .in1(unitate_centrala_1_cresc_60), .in2(poarta_sau_4_out_sau), .out_sau(poarta_sau_6_out_sau));
  Numarator_60 Num_60_alarma (
    .clk(unitate_centrala_1_cresc_60), .reset(Reset_out), .enable_60(unitate_centrala_1_en_set_al),
    .enable_24(out_1), .out_60(Num_60_alarma_out_60));
  Numarator_24 Num_24_alarma (
    .clk(unitate_centrala_1_cresc_24), .reset(Reset_out), .enable_24(unitate_centrala_1_en_set_al),
    .out_24(Num_24_alarma_out_24));
  Numarator_60 numarator_60_1 (
    .clk(poarta_sau_6_out_sau), .reset(Reset_out), .enable_60(poarta_sau_3_out_sau),
    .enable_24(numarator_60_1_enable_24), .out_60(numarator_60_1_out_60));
  Numarator_24 Num_24_ora (
    .clk(poarta_sau_5_out_sau), .reset(Reset_out), .enable_24(poarta_sau_3_out_sau),
    .out_24(Num_24_ora_out_24));
  Registru_6biti registru_6biti_1 (
    .reset(Reset_out), .clk(unitate_centrala_1_ok_set_al), .in_6(Num_60_alarma_out_60),
    .out_6(registru_6biti_1_out_6));
  Registru_5biti registru_5biti_1 (
    .reset(Reset_out), .clk(unitate_centrala_1_ok_set_al), .in_5(Num_24_alarma_out_24),
    .out_5(registru_5biti_1_out_5));
  comp_6b comp_6b_1 (.in1_6b(registru_6biti_1_out_6), .in2_6b(numarator_60_1_out_60), .cmp_6b(comp_6b_1_cmp_6b));
  comp_5b comp_5b_1 (.in1_5b(registru_5biti_1_out_5), .in2_5b(Num_24_ora_out_24), .cmp_5b(comp_5b_1_cmp_5b));
  LED Sunet_alarma (.in(poarta_si_2_si_out));
  Poarta_si poarta_si_2 (
    .in1(comp_6b_1_cmp_6b), .in2(comp_5b_1_cmp_5b), .in3(unitate_centrala_1_alarma_set),
    .si_out(poarta_si_2_si_out));
  Mux_2_la_1_5b mux_2_la_1_5b_1 (
    .in1(Num_24_alarma_out_24), .in2(Num_24_ora_out_24), .sel(unitate_centrala_1_en_set_al),
    .out5(mux_2_la_1_5b_1_out5));
  Mux_2_la_1_6b mux_2_la_1_6b_1 (
    .in1(Num_60_alarma_out_60), .in2(numarator_60_1_out_60), .sel(unitate_centrala_1_en_set_al),
    .out6(mux_2_la_1_6b_1_out6));
  convertor convertor_1 (
    .Bin_num({3'b000, mux_2_la_1_5b_1_out5}), .Unit(convertor_1_unit), .Decimal(convertor_1_decimal));
  convertor convertor_2 (
    .Bin_num({2'b00, mux_2_la_1_6b_1_out6}), .Unit(convertor_2_unit), .Decimal(convertor_2_decimal));
  hex2_7seg hex2_7seg_1 (.hex_in(convertor_1_unit), .a_b_c_d_e_f_g(hex2_7seg_1_a_b_c_d_e_f_g));
  hex2_7seg hex2_7seg_2 (.hex_in(convertor_1_decimal), .a_b_c_d_e_f_g(hex2_7seg_2_a_b_c_d_e_f_g));
  hex2_7seg hex2_7seg_3 (.hex_in(convertor_2_unit), .a_b_c_d_e_f_g(hex2_7seg_3_a_b_c_d_e_f_g));
  hex2_7seg hex2_7seg_4 (.hex_in(convertor_2_decimal), .a_b_c_d_e_f_g(hex2_7seg_4_a_b_c_d_e_f_g));
  _7_Segment_Display #(.active("false"), .decimalPoint("false")) u_7_segment_display_1 (
    .g(hex2_7seg_2_a_b_c_d_e_f_g[0]), .f(hex2_7seg_2_a_b_c_d_e_f_g[1]), .a(hex2_7seg_2_a_b_c_d_e_f_g[6]),
    .b(hex2_7seg_2_a_b_c_d_e_f_g[5]), .e(hex2_7seg_2_a_b_c_d_e_f_g[2]), .d(hex2_7seg_2_a_b_c_d_e_f_g[3]),
    .c(hex2_7seg_2_a_b_c_d_e_f_g[4]));
  _7_Segment_Display #(.active("false"), .decimalPoint("false")) u_7_segment_display_2 (
    .g(hex2_7seg_1_a_b_c_d_e_f_g[0]), .f(hex2_7seg_1_a_b_c_d_e_f_g[1]), .a(hex2_7seg_1_a_b_c_d_e_f_g[6]),
    .b(hex2_7seg_1_a_b_c_d_e_f_g[5]), .e(hex2_7seg_1_a_b_c_d_e_f_g[2]), .d(hex2_7seg_1_a_b_c_d_e_f_g[3]),
    .c(hex2_7seg_1_a_b_c_d_e_f_g[4]));
  _7_Segment_Display #(.active("false"), .decimalPoint("false")) u_7_segment_display_3 (
    .g(hex2_7seg_4_a_b_c_d_e_f_g[0]), .f(hex2_7seg_4_a_b_c_d_e_f_g[1]), .a(hex2_7seg_4_a_b_c_d_e_f_g[6]),
    .b(hex2_7seg_4_a_b_c_d_e_f_g[5]), .e(hex2_7seg_4_a_b_c_d_e_f_g[2]), .d(hex2_7seg_4_a_b_c_d_e_f_g[3]),
    .c(hex2_7seg_4_a_b_c_d_e_f_g[4]));
  _7_Segment_Display #(.active("false"), .decimalPoint("false")) u_7_segment_display_4 (
    .g(hex2_7seg_3_a_b_c_d_e_f_g[0]), .f(hex2_7seg_3_a_b_c_d_e_f_g[1]), .a(hex2_7seg_3_a_b_c_d_e_f_g[6]),
    .b(hex2_7seg_3_a_b_c_d_e_f_g[5]), .e(hex2_7seg_3_a_b_c_d_e_f_g[2]), .d(hex2_7seg_3_a_b_c_d_e_f_g[3]),
    .c(hex2_7seg_3_a_b_c_d_e_f_g[4]));
endmodule

// VHDL entity Numarator_24, as the project stores it:
--------------------------------------------------------------------------------
-- Project :
-- File    :
-- Autor   :
-- Date    :
--
--------------------------------------------------------------------------------
-- Description :
--
--------------------------------------------------------------------------------

LIBRARY ieee;
USE ieee.std_logic_1164.all;
USE ieee.numeric_std.ALL;

ENTITY Numarator_24 IS
  PORT (
  		clk: in std_logic;
        	reset: in std_logic;
        	enable_24: in std_logic;
        	out_24: out std_logic_vector(4 downto 0)
    );
END Numarator_24;

--------------------------------------------------------------------------------
--Complete your VHDL description below
--------------------------------------------------------------------------------

ARCHITECTURE TypeArchitecture OF Numarator_24 IS

signal count: std_logic_vector(4 downto 0) := (others => '0');

BEGIN
process (clk, reset)
    begin
        if reset = '1' then
            count <= "00000";
        
        elsif rising_edge(clk) and enable_24 = '1' then
            if count = "10111" then
                count <= "00000";
            else
                count <= std_logic_vector(unsigned(count) + 1);
            end if;
        end if;
    end process;

out_24 <= std_logic_vector(count);

END TypeArchitecture;

// VHDL entity Numarator_60, as the project stores it:
--------------------------------------------------------------------------------
-- Project :
-- File    :
-- Autor   :
-- Date    :
--
--------------------------------------------------------------------------------
-- Description :
--
--------------------------------------------------------------------------------

LIBRARY ieee;
USE ieee.std_logic_1164.all;
USE ieee.numeric_std.all;

ENTITY Numarator_60 IS
  PORT (
  		clk: in std_logic;
        	reset: in std_logic;
        	enable_60: in std_logic;
        	enable_24: out std_logic;
        	out_60: out std_logic_vector(5 downto 0)
    );
END Numarator_60;

--------------------------------------------------------------------------------
--Complete your VHDL description below
--------------------------------------------------------------------------------

ARCHITECTURE TypeArchitecture OF Numarator_60 IS

SIGNAL count : STD_LOGIC_VECTOR(5 DOWNTO 0) := (OTHERS => '0');
signal en_aux : std_logic := '0';

BEGIN
	
	process (clk, reset)
    	begin
 		if reset = '1' then
         		count <= "000000";
      		en_aux <= '0';
        	
        	elsif rising_edge(clk) and enable_60 = '1' then
          	if count = "111011" then
               	 count <= "000000";
               	 en_aux <= '1';
               	 
            	else
               	 count <= std_logic_vector(unsigned(count) + 1);
               	 en_aux <= '0';
            	end if;
        	end if;
    end process;

enable_24 <= en_aux;
out_60 <= count;

END TypeArchitecture;

// VHDL entity Registru_5biti, as the project stores it:
--------------------------------------------------------------------------------
-- Project :
-- File    :
-- Autor   :
-- Date    :
--
--------------------------------------------------------------------------------
-- Description :
--
--------------------------------------------------------------------------------

LIBRARY ieee;
USE ieee.std_logic_1164.all;
use ieee.numeric_std.all;
use ieee.numeric_std_unsigned.all;

ENTITY Registru_5biti IS
  PORT (
        	reset: in std_logic;
        	clk: in std_logic;
        	in_5: in std_logic_vector(4 downto 0);
	     out_5: out std_logic_vector(4 downto 0)
    );
END Registru_5biti;

--------------------------------------------------------------------------------
--Complete your VHDL description below
--------------------------------------------------------------------------------

ARCHITECTURE TypeArchitecture OF Registru_5biti IS

signal reg: std_logic_vector(4 downto 0) := (others => '0');

BEGIN

	process (clk, reset)
    		begin
        		if reset = '1' then
            		reg <= "00000";
        		elsif rising_edge(clk) then
                	reg <= in_5;
        		end if;
    end process;

    out_5 <= reg;

END TypeArchitecture;

// VHDL entity Registru_6biti, as the project stores it:
--------------------------------------------------------------------------------
-- Project :
-- File    :
-- Autor   :
-- Date    :
--
--------------------------------------------------------------------------------
-- Description :
--
--------------------------------------------------------------------------------

LIBRARY ieee;
USE ieee.std_logic_1164.all;
use ieee.numeric_std.all;
use ieee.numeric_std_unsigned.all;

ENTITY Registru_6biti IS
  PORT (
  		reset: in std_logic;
        	clk: in std_logic;
        	in_6: in std_logic_vector(5 downto 0);
	     out_6: out std_logic_vector(5 downto 0)
    );
END Registru_6biti;

--------------------------------------------------------------------------------
--Complete your VHDL description below
--------------------------------------------------------------------------------

ARCHITECTURE TypeArchitecture OF Registru_6biti IS

signal reg: std_logic_vector(5 downto 0) := (others => '0');

BEGIN

	process (clk, reset)
    		begin
        		if reset = '1' then
            		reg <= "000000";
        		elsif rising_edge(clk) then
                	reg <= std_logic_vector(unsigned(in_6) + 1);
        		end if;
    end process;

    out_6 <= reg;

END TypeArchitecture;

// VHDL entity div_frecv, as the project stores it:
--------------------------------------------------------------------------------
-- Project :
-- File    :
-- Autor   :
-- Date    :
--
--------------------------------------------------------------------------------
-- Description :
--
--------------------------------------------------------------------------------

LIBRARY ieee;
USE ieee.std_logic_1164.all;
USE ieee.std_logic_unsigned.all;

ENTITY div_frecv IS
  PORT (
    clock      : IN  std_logic;
    div_clk    : OUT std_logic
    );
END div_frecv;

--------------------------------------------------------------------------------
--Complete your VHDL description below
--------------------------------------------------------------------------------

ARCHITECTURE TypeArchitecture OF div_frecv IS

signal tmp:std_logic_vector (6 downto 0):=(others =>'0');

BEGIN

process(clock)
begin
	if(rising_edge(clock)) then
		if tmp = ("1100011") then 
				tmp <= "0000000";
			elsif (tmp <= "0110001") then
				tmp <= tmp + 1;
				div_clk <= '0';
			else div_clk <= '1';
				tmp <= tmp + 1;
		end if;
	end if;	
end process;

END TypeArchitecture;

// VHDL entity comp_5b, as the project stores it:
--------------------------------------------------------------------------------
-- Project :
-- File    :
-- Autor   :
-- Date    :
--
--------------------------------------------------------------------------------
-- Description :
--
--------------------------------------------------------------------------------

LIBRARY ieee;
USE ieee.std_logic_1164.all;

ENTITY comp_5b IS
  PORT (
  	in1_5b, in2_5b : in std_logic_vector(4 downto 0);
  	cmp_5b : out std_logic
    );
END comp_5b;

--------------------------------------------------------------------------------
--Complete your VHDL description below
--------------------------------------------------------------------------------

ARCHITECTURE TypeArchitecture OF comp_5b IS

BEGIN

	cmp_5b <= '1' when in1_5b = in2_5b else '0';

END TypeArchitecture;

// VHDL entity comp_6b, as the project stores it:
--------------------------------------------------------------------------------
-- Project :
-- File    :
-- Autor   :
-- Date    :
--
--------------------------------------------------------------------------------
-- Description :
--
--------------------------------------------------------------------------------

LIBRARY ieee;
USE ieee.std_logic_1164.all;

ENTITY comp_6b IS
  PORT (
  	in1_6b, in2_6b : in std_logic_vector(5 downto 0);
  	cmp_6b : out std_logic
    );
END comp_6b;

--------------------------------------------------------------------------------
--Complete your VHDL description below
--------------------------------------------------------------------------------

ARCHITECTURE TypeArchitecture OF comp_6b IS

BEGIN

	cmp_6b <= '1' when in1_6b = in2_6b else '0';

END TypeArchitecture;

// VHDL entity unitate_centrala, as the project stores it:
--------------------------------------------------------------------------------
-- Project :
-- File    :
-- Autor   :
-- Date    :
--
--------------------------------------------------------------------------------
-- Description :
--
--------------------------------------------------------------------------------

LIBRARY ieee;
USE ieee.std_logic_1164.all;

ENTITY unitate_centrala IS
  PORT (
  	pornire, oprire, setare_ora, alarma, radio, ok, reset, ora, minut, clk, ring : in std_logic;
  	led_radio, en_set_al, en_set_ora, cresc_60, cresc_24, ok_set_al, led_on, alarma_set: out std_logic
    );
END unitate_centrala;

--------------------------------------------------------------------------------
--Complete your VHDL description below
--------------------------------------------------------------------------------

ARCHITECTURE TypeArchitecture OF unitate_centrala IS

type STATE_T is (Off, Idle, State_set_al, State_set_hour);
signal STATE, NXSTATE: STATE_T;
signal aux_radio : std_logic := '0';
signal aux_alarma : std_logic := '0';

BEGIN

UPDATE_STATE: process (Reset, Clk)
			begin
				if (reset = '1') then
					STATE <= Off;
				elsif clk'EVENT and clk = '1' then
					STATE <= NXSTATE;
				end if;
			end process UPDATE_STATE;


TRANSITIONS: process (STATE, oprire, pornire, setare_ora, alarma, ok)
			begin
				case STATE is
					when Off => 	if pornire = '1' then NXSTATE<=Idle;
								else NXSTATE <= Off;
								end if;
								
					when Idle => 	if oprire = '1' then NXSTATE <= Off;
								elsif setare_ora = '1' then
								NXSTATE <= State_set_hour;
								elsif alarma = '1' then
                    				NXSTATE <= State_set_al;
								else
                    				NXSTATE <= Idle;
                					end if;
                					
					when State_set_hour => 	if ok = '1' then
                    						NXSTATE <= Idle;
                							else
                    						NXSTATE <= State_set_hour;
                							end if;			

					when State_set_al => 	if ok = '1' then
										NXSTATE <= Idle;
										else
										NXSTATE <= State_set_al;
										end if;
				end case;
			end process TRANSITIONS;


Outputs: process (STATE, pornire, oprire, setare_ora, alarma, ok, radio, ora, minut, ring)
		begin
			case STATE is
			
				when Off => 	led_on <= '0';
							led_radio <= '0';
							en_set_al <= '0';
							en_set_ora <= '0';
							cresc_60 <= '0';
							cresc_24 <= '0';
							ok_set_al <= '0';
							aux_alarma <= '0';
							aux_radio <= '0';
							alarma_set <= '0';
							
				when Idle => 	led_on <= '1';
							en_set_al <= '0';
							en_set_ora <= '0';
							if radio = '1' then
                					if aux_radio = '0' then
                    					aux_radio <= '1';
                					else
                    					aux_radio <= '0';
								end if;
							end if;
							led_radio <= aux_radio;
							if ring = '1' then
								if aux_alarma = '0' then
                    					aux_alarma <= '1';
                					else
                    					aux_alarma <= '0';
								end if;
							end if;
							alarma_set <= aux_alarma;	
								
							
				when State_set_hour => 	en_set_ora <= '1';
				
									if ora = '1' then
										cresc_24 <= '1';
									else
										cresc_24 <= '0';
									end if;
									if minut = '1' then
										cresc_60 <= '1';
									else
										cresc_60 <= '0';
									end if;
									
				when State_set_al =>	en_set_al <= '1';
									if ora = '1' then
										cresc_24 <= '1';
										ok_set_al <= '1';
									else
										cresc_24 <= '0';
										ok_set_al <= '0';
									end if;
									if minut = '1' then
										cresc_60 <= '1';
										ok_set_al <= '1';
									else
										cresc_60 <= '0';
										ok_set_al <= '0';
									end if;						
				
			end case;
		end process Outputs;
		
END TypeArchitecture;

// VHDL entity hex2_7seg, as the project stores it:
--------------------------------------------------------------------------------
-- Project :
-- File    :
-- Autor   :
-- Date    :
--
--------------------------------------------------------------------------------
-- Description :
--
--------------------------------------------------------------------------------

LIBRARY ieee;
USE ieee.std_logic_1164.all;

ENTITY hex2_7seg IS
  PORT (
  	hex_in : in std_logic_vector(3 downto 0);
  	a_b_c_d_e_f_g : out std_logic_vector(6 downto 0)
    );
END hex2_7seg;

--------------------------------------------------------------------------------
--Complete your VHDL description below
--------------------------------------------------------------------------------

ARCHITECTURE TypeArchitecture OF hex2_7seg IS

BEGIN

a_b_c_d_e_f_g <=   "0000001" when hex_in = x"0" else
                   "1001111" when hex_in = x"1" else
                   "0010010" when hex_in = x"2" else
                   "0000110" when hex_in = x"3" else
                   "1001100" when hex_in = x"4" else
                   "0100100" when hex_in = x"5" else
                   "0100000" when hex_in = x"6" else
                   "0001111" when hex_in = x"7" else
                   "0000000" when hex_in = x"8" else
                   "0000100" when hex_in = x"9" else
                   "0001000" when hex_in = x"A" else
                   "1100000" when hex_in = x"B" else
                   "0110000" when hex_in = x"C" else
                   "1000010" when hex_in = x"D" else 
                   "0110000" when hex_in = x"E" else
                   "0111000" when hex_in = x"F" else
                   "1111111";

END TypeArchitecture;

// VHDL entity Poarta_si, as the project stores it:
--------------------------------------------------------------------------------
-- Project :
-- File    :
-- Autor   :
-- Date    :
--
--------------------------------------------------------------------------------
-- Description :
--
--------------------------------------------------------------------------------

LIBRARY ieee;
USE ieee.std_logic_1164.all;

ENTITY Poarta_si IS
  PORT (
  	in1, in2, in3: in std_logic;
  	si_out : out std_logic
    );
END Poarta_si;

--------------------------------------------------------------------------------
--Complete your VHDL description below
--------------------------------------------------------------------------------

ARCHITECTURE TypeArchitecture OF Poarta_si IS

BEGIN

si_out <= in1 AND in2 AND in3;

END TypeArchitecture;

// VHDL entity convertor, as the project stores it:
--------------------------------------------------------------------------------
-- Project :
-- File    :
-- Autor   :
-- Date    :
--
--------------------------------------------------------------------------------
-- Description :
--
--------------------------------------------------------------------------------

LIBRARY ieee;
USE ieee.std_logic_1164.all;
USE ieee.std_logic_1164.all;
USE ieee.std_logic_unsigned.all;
USE ieee.std_logic_arith.all;

ENTITY convertor IS
  PORT (
  		Bin_num: in std_logic_vector(7 downto 0);
  		Unit: out std_logic_vector(3 downto 0);
  		Decimal: out std_logic_vector(3 downto 0)  
    );
END convertor;

--------------------------------------------------------------------------------
--Complete your VHDL description below
--------------------------------------------------------------------------------

ARCHITECTURE TypeArchitecture OF convertor IS

signal num_int: integer:=0;
signal u,z: integer:=0;

BEGIN


	num_int<=conv_integer(bin_num);
	z<=num_int / 10;
	u<=num_int rem 10;
	process(u)
	begin
		case u is
		when 0 => unit <= x"0";
		when 1 => unit <= x"1";
		when 2 => unit <= x"2";
		when 3 => unit <= x"3";
		when 4 => unit <= x"4";
		when 5 => unit <= x"5";
		when 6 => unit <= x"6";
		when 7 => unit <= x"7";
		when 8 => unit <= x"8";
		when 9 => unit <= x"9";
		when others => unit <=x"f";
		end case;
	end process;
	process(z)
	begin
		case z is
		when 0 => Decimal <= x"0";
		when 1 => Decimal <= x"1";
		when 2 => Decimal <= x"2";
		when 3 => Decimal <= x"3";
		when 4 => Decimal <= x"4";
		when 5 => Decimal <= x"5";
		when 6 => Decimal <= x"6";
		when 7 => Decimal <= x"7";
		when 8 => Decimal <= x"8";
		when 9 => Decimal <= x"9";
		when others => Decimal <=x"f";
		end case;
	end process;


END TypeArchitecture;

// VHDL entity Poarta_sau, as the project stores it:
--------------------------------------------------------------------------------
-- Project :
-- File    :
-- Autor   :
-- Date    :
--
--------------------------------------------------------------------------------
-- Description :
--
--------------------------------------------------------------------------------

LIBRARY ieee;
USE ieee.std_logic_1164.all;

ENTITY Poarta_sau IS
  PORT (
	in1, in2 : in std_logic;
	out_sau : out std_logic
    );
END Poarta_sau;

--------------------------------------------------------------------------------
--Complete your VHDL description below
--------------------------------------------------------------------------------

ARCHITECTURE TypeArchitecture OF Poarta_sau IS

BEGIN

out_sau <= in2 OR in1;

END TypeArchitecture;

// VHDL entity num_secunde, as the project stores it:
--------------------------------------------------------------------------------
-- Project :
-- File    :
-- Autor   :
-- Date    :
--
--------------------------------------------------------------------------------
-- Description :
--
--------------------------------------------------------------------------------

LIBRARY ieee;
USE ieee.std_logic_1164.all;
USE ieee.numeric_std.all;

ENTITY num_secunde IS
  PORT (
  		clk: in std_logic;
        	reset: in std_logic;
        	enable: out std_logic;
        	out_60: out std_logic_vector(5 downto 0)
    );
END num_secunde;

--------------------------------------------------------------------------------
--Complete your VHDL description below
--------------------------------------------------------------------------------

ARCHITECTURE TypeArchitecture OF num_secunde IS

SIGNAL count : STD_LOGIC_VECTOR(5 DOWNTO 0) := (OTHERS => '0');
signal en_aux : std_logic := '0';

BEGIN

process (clk, reset)
    	begin

 		if reset = '1' then
         		count <= "000000";
      		en_aux <= '0';
        	
        	elsif rising_edge(clk) then
          	if count = "111011" then
               	 count <= "000000";
               	 en_aux <= '1';
               	 
            	else
               	 count <= std_logic_vector(unsigned(count) + 1);
               	 en_aux <= '0';
            	end if;
        	end if;
    end process;

enable <= en_aux;
out_60 <= count;

END TypeArchitecture;

// VHDL entity si_2, as the project stores it:
--------------------------------------------------------------------------------
-- Project :
-- File    :
-- Autor   :
-- Date    :
--
--------------------------------------------------------------------------------
-- Description :
--
--------------------------------------------------------------------------------

LIBRARY ieee;
USE ieee.std_logic_1164.all;

ENTITY si_2 IS
  PORT (
  	in1, in2 : in std_logic;
  	out2 : out std_logic
    );
END si_2;

--------------------------------------------------------------------------------
--Complete your VHDL description below
--------------------------------------------------------------------------------

ARCHITECTURE TypeArchitecture OF si_2 IS

BEGIN

out2 <= in1 AND in2;

END TypeArchitecture;

// VHDL entity poarta_nu, as the project stores it:
--------------------------------------------------------------------------------
-- Project :
-- File    :
-- Autor   :
-- Date    :
--
--------------------------------------------------------------------------------
-- Description :
--
--------------------------------------------------------------------------------

LIBRARY ieee;
USE ieee.std_logic_1164.all;

ENTITY poarta_nu IS
  PORT (
  	a : in std_logic;
  	b : out std_logic
    );
END poarta_nu;

--------------------------------------------------------------------------------
--Complete your VHDL description below
--------------------------------------------------------------------------------

ARCHITECTURE TypeArchitecture OF poarta_nu IS

BEGIN

b <= NOT a;

END TypeArchitecture;

// VHDL entity Mux_2_la_1_5b, as the project stores it:
--------------------------------------------------------------------------------
-- Project :
-- File    :
-- Autor   :
-- Date    :
--
--------------------------------------------------------------------------------
-- Description :
--
--------------------------------------------------------------------------------

LIBRARY ieee;
USE ieee.std_logic_1164.all;

ENTITY Mux_2_la_1_5b IS
  PORT (
  		in1, in2 : in std_logic_vector(4 downto 0);
  		sel : in std_logic;
  		out5 : out std_logic_vector(4 downto 0)
    );
END Mux_2_la_1_5b;

--------------------------------------------------------------------------------
--Complete your VHDL description below
--------------------------------------------------------------------------------

ARCHITECTURE TypeArchitecture OF Mux_2_la_1_5b IS

BEGIN

out5 <= in1 WHEN sel = '1' ELSE in2;

END TypeArchitecture;

// VHDL entity Mux_2_la_1_6b, as the project stores it:
--------------------------------------------------------------------------------
-- Project :
-- File    :
-- Autor   :
-- Date    :
--
--------------------------------------------------------------------------------
-- Description :
--
--------------------------------------------------------------------------------

LIBRARY ieee;
USE ieee.std_logic_1164.all;

ENTITY Mux_2_la_1_6b IS
  PORT (
 		in1, in2 : in std_logic_vector(5 downto 0);
  		sel : in std_logic;
  		out6 : out std_logic_vector(5 downto 0)
    );
END Mux_2_la_1_6b;

--------------------------------------------------------------------------------
--Complete your VHDL description below
--------------------------------------------------------------------------------

ARCHITECTURE TypeArchitecture OF Mux_2_la_1_6b IS

BEGIN

out6 <= in1 WHEN sel = '1' ELSE in2;


END TypeArchitecture;
